// Logisim project C1.circ as structural Verilog: 1 circuit, main circuit main
module main (
  input  A,
  input  B,
  input  C,
  output E,
  output D,
  output G,
  output F
);

  or or_1 (E, A, B);
  and and_1 (F, B, C);
  xor xor_1 (G, E, F);
  not not_1 (D, G);
endmodule
